# Fritzing sketch PotentiometerRGBledUNO9V (saved by Fritzing 0.9.2b)
breadboards: 1

parts:
  RGB_led = RGB LED - (4 legs) [package="5 mm [THT]"]
  BAT1 = BC9VPC [package=bc9vpc]
  Part3 = Arduino Uno (Rev3) - ICSP
  part = Resistor [tolerance=±5% resistance=330 package=THT]
  part_2 = Resistor [tolerance=±5% resistance=330 package=THT]
  part_3 = Resistor [tolerance=±5% resistance=330 package=THT]
  R4 = Rotary Potentiometer (Large) [maximum_resistance=100kΩ package=THT]

nets:
  N1: RGB_led.red_cathode, part_3.Pin_0
  N2: RGB_led.common_anode, Part3.5V, R4.leg2
  N3: RGB_led.green_cathode, part_2.Pin_0
  N4: RGB_led.blue_cathode, part.Pin_0
  N5: BAT1.V+, Part3.VIN
  N6: BAT1.V-, Part3.GND, R4.leg1
  N7: Part3.A0, R4.wiper
  N8: Part3.D3_PWM, part.Pin_1
  N9: Part3.D5_PWM, part_2.Pin_1
  N10: Part3.D6_PWM, part_3.Pin_1
